// Logisim project CPU_FFFinal.circ as structural Verilog: 6 circuits, main circuit implementation
module implementation (
  input  [15:0] Instruction_In,
  input  ClkIn,
  input  in_3,
  output out_4,
  output [4:0] Instruction_Address_Out,
  output [3:0] Reg0_Out,
  output [3:0] Reg1_Out,
  output [3:0] Reg2_Out,
  output [3:0] Reg3_Out,
  output [3:0] Reg4_Out,
  output [3:0] Reg5_Out,
  output [3:0] Reg6_Out,
  output [3:0] Reg7_Out,
  output [3:0] Reg8_Out,
  output [3:0] Reg9_Out,
  output [3:0] Reg10_Out,
  output [3:0] Reg11_Out,
  output [3:0] Reg12_Out,
  output [3:0] Reg13_Out,
  output [3:0] Reg14_Out,
  output [3:0] Reg15_Out
);

  wire and_1_out, opcode_decoder_1_imme, opcode_decoder_1_reg_wirte_in, STOP;
  wire [3:0] A_Value, alu_1_data_in, B_Value, ir_1_a, ir_1_b_imme, ir_1_c, ir_1_opcode, multiplexer_2_out;

  and and_1 (and_1_out, ClkIn, in_3);
  Multiplexer multiplexer_1 (.in0(ClkIn), .in1(and_1_out), .out(out_4), .sel(STOP));
  IR ir_1 (.inst(Instruction_In), .a(ir_1_a), .b_imme(ir_1_b_imme), .c(ir_1_c), .opcode(ir_1_opcode));
  OpCode_decoder opcode_decoder_1 (
    .opcode(ir_1_opcode), .STOP(STOP), .Reg_Wirte_in(opcode_decoder_1_reg_wirte_in),
    .imme(opcode_decoder_1_imme));
  Multiplexer #(.width(4)) multiplexer_2 (
    .in0(B_Value), .in1(ir_1_b_imme), .out(multiplexer_2_out), .sel(opcode_decoder_1_imme));
  PC pc_1 (.stop(STOP), .Clock(out_4), .inst(Instruction_Address_Out));
  ALU alu_1 (.a(A_Value), .b(multiplexer_2_out), .Opcode(ir_1_opcode), .Data_in(alu_1_data_in));  // open: in_1
  RegFile regfile_1 (
    .A_Sel_In(ir_1_a), .B_Sel_In(ir_1_b_imme), .C_Sel_In(ir_1_c), .Data_In(alu_1_data_in),
    .Reg_Write_In(opcode_decoder_1_reg_wirte_in), .clk_in(out_4), .A_Out(A_Value), .B_Out(B_Value),
    .Reg0_Out(Reg0_Out), .Reg1_Out(Reg1_Out), .Reg2_Out(Reg2_Out), .Reg3_Out(Reg3_Out), .Reg4_Out(Reg4_Out),
    .Reg5_Out(Reg5_Out), .Reg6_Out(Reg6_Out), .Reg7_Out(Reg7_Out), .Reg8_Out(Reg8_Out), .Reg9_Out(Reg9_Out),
    .Reg10_Out(Reg10_Out), .Reg11_Out(Reg11_Out), .Reg12_Out(Reg12_Out), .Reg13_Out(Reg13_Out),
    .Reg14_Out(Reg14_Out), .Reg15_Out(Reg15_Out));

  // Other names for the same wires on the sheet: Clk = out_4; Instruction[15:0] = Instruction_In;
  //   Instruction_Address[4:0] = Instruction_Address_Out; Reg0[3:0] = Reg0_Out; Reg1[3:0] = Reg1_Out;
  //   Reg2[3:0] = Reg2_Out; Reg3[3:0] = Reg3_Out; Reg4[3:0] = Reg4_Out; Reg5[3:0] = Reg5_Out; Reg6[3:0] = Reg6_Out;
  //   Reg7[3:0] = Reg7_Out; Reg8[3:0] = Reg8_Out; Reg9[3:0] = Reg9_Out; Reg10[3:0] = Reg10_Out;
  //   Reg11[3:0] = Reg11_Out; Reg12[3:0] = Reg12_Out; Reg13[3:0] = Reg13_Out; Reg14[3:0] = Reg14_Out;
  //   Reg15[3:0] = Reg15_Out

  // Notes on the sheet:
  //   STOP instruction --> kill the clock
endmodule

module RegFile (
  input  [3:0] A_Sel_In,
  input  [3:0] B_Sel_In,
  input  [3:0] C_Sel_In,
  input  [3:0] Data_In,
  input  Reg_Write_In,
  input  clk_in,
  output [3:0] A_Out,
  output [3:0] B_Out,
  output [3:0] Reg0_Out,
  output [3:0] Reg1_Out,
  output [3:0] Reg2_Out,
  output [3:0] Reg3_Out,
  output [3:0] Reg4_Out,
  output [3:0] Reg5_Out,
  output [3:0] Reg6_Out,
  output [3:0] Reg7_Out,
  output [3:0] Reg8_Out,
  output [3:0] Reg9_Out,
  output [3:0] Reg10_Out,
  output [3:0] Reg11_Out,
  output [3:0] Reg12_Out,
  output [3:0] Reg13_Out,
  output [3:0] Reg14_Out,
  output [3:0] Reg15_Out
);

  wire Reg_Write0, Reg_Write1, Reg_Write2, Reg_Write3, Reg_Write4, Reg_Write5, Reg_Write6, Reg_Write7,
       Reg_Write8, Reg_Write9, Reg_Write10, Reg_Write11, Reg_Write12, Reg_Write13, Reg_Write14, Reg_Write15;

  Demultiplexer #(.enable("true"), .select(4)) demultiplexer_1 (
    .out0(Reg_Write0), .out1(Reg_Write1), .out2(Reg_Write2), .out3(Reg_Write3), .out4(Reg_Write4),
    .out5(Reg_Write5), .out6(Reg_Write6), .out7(Reg_Write7), .out8(Reg_Write8), .out9(Reg_Write9),
    .out10(Reg_Write10), .out11(Reg_Write11), .out12(Reg_Write12), .out13(Reg_Write13), .out14(Reg_Write14),
    .out15(Reg_Write15), .in(Reg_Write_In), .sel(C_Sel_In));  // open: en
  Register #(.width(4)) register_1 (.D(Data_In), .en(Reg_Write0), .clk(clk_in), .Q(Reg0_Out));  // open: clr
  Register #(.width(4)) register_2 (.D(Data_In), .en(Reg_Write4), .clk(clk_in), .Q(Reg4_Out));  // open: clr
  Register #(.width(4)) register_3 (.D(Data_In), .en(Reg_Write8), .clk(clk_in), .Q(Reg8_Out));  // open: clr
  Register #(.width(4)) register_4 (.D(Data_In), .en(Reg_Write12), .clk(clk_in), .Q(Reg12_Out));  // open: clr
  Register #(.width(4)) register_5 (.D(Data_In), .en(Reg_Write1), .clk(clk_in), .Q(Reg1_Out));  // open: clr
  Register #(.width(4)) register_6 (.D(Data_In), .en(Reg_Write5), .clk(clk_in), .Q(Reg5_Out));  // open: clr
  Register #(.width(4)) register_7 (.D(Data_In), .en(Reg_Write9), .clk(clk_in), .Q(Reg9_Out));  // open: clr
  Register #(.width(4)) register_8 (.D(Data_In), .en(Reg_Write13), .clk(clk_in), .Q(Reg13_Out));  // open: clr
  Register #(.width(4)) register_9 (.D(Data_In), .en(Reg_Write2), .clk(clk_in), .Q(Reg2_Out));  // open: clr
  Register #(.width(4)) register_10 (.D(Data_In), .en(Reg_Write6), .clk(clk_in), .Q(Reg6_Out));  // open: clr
  Register #(.width(4)) register_11 (.D(Data_In), .en(Reg_Write10), .clk(clk_in), .Q(Reg10_Out));  // open: clr
  Register #(.width(4)) register_12 (.D(Data_In), .en(Reg_Write14), .clk(clk_in), .Q(Reg14_Out));  // open: clr
  Register #(.width(4)) register_13 (.D(Data_In), .en(Reg_Write3), .clk(clk_in), .Q(Reg3_Out));  // open: clr
  Register #(.width(4)) register_14 (.D(Data_In), .en(Reg_Write7), .clk(clk_in), .Q(Reg7_Out));  // open: clr
  Register #(.width(4)) register_15 (.D(Data_In), .en(Reg_Write11), .clk(clk_in), .Q(Reg11_Out));  // open: clr
  Register #(.width(4)) register_16 (.D(Data_In), .en(Reg_Write15), .clk(clk_in), .Q(Reg15_Out));  // open: clr
  Multiplexer #(.enable("true"), .select(4), .width(4)) multiplexer_1 (
    .in0(Reg0_Out), .in1(Reg1_Out), .in2(Reg2_Out), .in3(Reg3_Out), .in4(Reg4_Out), .in5(Reg5_Out),
    .in6(Reg6_Out), .in7(Reg7_Out), .in8(Reg8_Out), .in9(Reg9_Out), .in10(Reg10_Out), .in11(Reg11_Out),
    .in12(Reg12_Out), .in13(Reg13_Out), .in14(Reg14_Out), .in15(Reg15_Out), .out(A_Out), .sel(A_Sel_In));  // open: en
  Multiplexer #(.enable("true"), .select(4), .width(4)) multiplexer_2 (
    .in0(Reg0_Out), .in1(Reg1_Out), .in2(Reg2_Out), .in3(Reg3_Out), .in4(Reg4_Out), .in5(Reg5_Out),
    .in6(Reg6_Out), .in7(Reg7_Out), .in8(Reg8_Out), .in9(Reg9_Out), .in10(Reg10_Out), .in11(Reg11_Out),
    .in12(Reg12_Out), .in13(Reg13_Out), .in14(Reg14_Out), .in15(Reg15_Out), .out(B_Out), .sel(B_Sel_In));  // open: en

  // Other names for the same wires on the sheet: A[3:0] = A_Out; A_Sel[3:0] = A_Sel_In; B[3:0] = B_Out;
  //   B_Sel[3:0] = B_Sel_In; C_Sel[3:0] = C_Sel_In; clk = clk_in; Data[3:0] = Data_In; Reg0[3:0] = Reg0_Out;
  //   Reg1[3:0] = Reg1_Out; Reg2[3:0] = Reg2_Out; Reg3[3:0] = Reg3_Out; Reg4[3:0] = Reg4_Out; Reg5[3:0] = Reg5_Out;
  //   Reg6[3:0] = Reg6_Out; Reg7[3:0] = Reg7_Out; Reg8[3:0] = Reg8_Out; Reg9[3:0] = Reg9_Out; Reg10[3:0] = Reg10_Out;
  //   Reg11[3:0] = Reg11_Out; Reg12[3:0] = Reg12_Out; Reg13[3:0] = Reg13_Out; Reg14[3:0] = Reg14_Out;
  //   Reg15[3:0] = Reg15_Out; Reg_Write = Reg_Write_In
endmodule

module ALU (
  input  [3:0] in_1,
  input  [3:0] a,
  input  [3:0] b,
  input  [3:0] Opcode,
  output [3:0] Data_in
);

  wire adder_1_cout, adder_2_cout, adder_3_cout, subtractor_1_bout, subtractor_2_bout, subtractor_3_bout;
  wire [3:0] adder_1_out, adder_5_out, and_1_out, not_1_out, or_1_out, subtractor_1_out, undriven,
       undriven_2, xor_1_out;

  Adder #(.width(1)) adder_1 (.a(a[0]), .b(b[0]), .out(adder_1_out[0]), .cout(adder_1_cout));  // open: cin
  Adder #(.width(1)) adder_2 (.a(a[1]), .b(b[1]), .out(adder_1_out[1]), .cin(adder_1_cout), .cout(adder_2_cout));
  Adder #(.width(1)) adder_3 (.a(a[2]), .b(b[2]), .out(adder_1_out[2]), .cin(adder_2_cout), .cout(adder_3_cout));
  Adder #(.width(1)) adder_4 (.a(a[3]), .b(b[3]), .out(adder_1_out[3]), .cin(adder_3_cout));  // open: cout
  Subtractor #(.width(1)) subtractor_1 (
    .a(a[0]), .b(b[0]), .out(subtractor_1_out[0]), .bout(subtractor_1_bout));  // open: bin
  Subtractor #(.width(1)) subtractor_2 (
    .a(a[1]), .b(b[1]), .out(subtractor_1_out[1]), .bin(subtractor_1_bout), .bout(subtractor_2_bout));
  Subtractor #(.width(1)) subtractor_3 (
    .a(a[2]), .b(b[2]), .out(subtractor_1_out[2]), .bin(subtractor_2_bout), .bout(subtractor_3_bout));
  Subtractor #(.width(1)) subtractor_4 (
    .a(a[3]), .b(b[3]), .out(subtractor_1_out[3]), .bin(subtractor_3_bout));  // open: bout
  and and_1 (and_1_out[0], a[0], b[0]);
  and and_2 (and_1_out[1], a[1], b[1]);
  and and_3 (and_1_out[2], a[2], b[2]);
  and and_4 (and_1_out[3], b[3], a[3]);
  or or_1 (or_1_out[0], a[0], b[0]);
  or or_2 (or_1_out[1], a[1], b[1]);
  or or_3 (or_1_out[2], a[2], b[2]);
  or or_4 (or_1_out[3], a[3], b[3]);
  xor xor_1 (xor_1_out[0], a[0], b[0]);
  xor xor_2 (xor_1_out[1], a[1], b[1]);
  xor xor_3 (xor_1_out[2], a[2], b[2]);
  xor xor_4 (xor_1_out[3], a[3], b[3]);
  not not_1 (not_1_out[0], a[0]);
  not not_2 (not_1_out[1], a[1]);
  not not_3 (not_1_out[2], a[2]);
  not not_4 (not_1_out[3], a[3]);
  Adder #(.width(4)) adder_5 (.a(not_1_out), .b(4'b0001), .out(adder_5_out));  // open: cin, cout
  Multiplexer #(.select(4), .width(4)) multiplexer_1 (
    .in0(undriven), .in1(undriven_2), .in2(adder_1_out), .in3(subtractor_1_out), .in4(and_1_out),
    .in5(or_1_out), .in6(xor_1_out), .in7(adder_1_out), .in8(subtractor_1_out), .in9(and_1_out),
    .in10(or_1_out), .in11(xor_1_out), .in12(adder_5_out), .in13(not_1_out), .in14(a), .in15(b),
    .out(Data_in), .sel(Opcode));

  // Notes on the sheet:
  //   ADD 000
  //   SUB 001
  //   AND 010
  //   OR 011
  //   XOR 100
  //   MOVE
  //   NOT
  //   NEGATE
endmodule

module OpCode_decoder (
  input  [3:0] opcode,
  output STOP,
  output Reg_Wirte_in,
  output imme
);

  wire decoder_1_out2, decoder_1_out3, decoder_1_out4, decoder_1_out5, decoder_1_out6, decoder_1_out7,
       decoder_1_out8, decoder_1_out9, decoder_1_out10, decoder_1_out11, decoder_1_out12, decoder_1_out13,
       decoder_1_out14, decoder_1_out15;

  Decoder #(.enable("false"), .select(4)) decoder_1 (
    .out1(STOP), .out2(decoder_1_out2), .out3(decoder_1_out3), .out4(decoder_1_out4), .out5(decoder_1_out5),
    .out6(decoder_1_out6), .out7(decoder_1_out7), .out8(decoder_1_out8), .out9(decoder_1_out9),
    .out10(decoder_1_out10), .out11(decoder_1_out11), .out12(decoder_1_out12), .out13(decoder_1_out13),
    .out14(decoder_1_out14), .out15(decoder_1_out15), .sel(opcode));  // open: out0
  or or_1 (imme, decoder_1_out7, decoder_1_out8, decoder_1_out9, decoder_1_out10, decoder_1_out11, decoder_1_out15);
  or or_2 (Reg_Wirte_in, decoder_1_out2, decoder_1_out3, decoder_1_out4, decoder_1_out5, decoder_1_out6, decoder_1_out7, decoder_1_out8, decoder_1_out10, decoder_1_out11, decoder_1_out12, decoder_1_out13, decoder_1_out14, decoder_1_out15, decoder_1_out9);
endmodule

module PC (
  input  stop,
  input  Clock,
  output [4:0] inst
);

  wire [4:0] adder_1_out, d_ff_1_q;

  D_Flip_Flop d_ff_1 (.D(inst[0]), .clk(Clock), .Q(d_ff_1_q[0]));  // open: Qn, preset, reset
  D_Flip_Flop d_ff_2 (.D(inst[1]), .clk(Clock), .Q(d_ff_1_q[1]));  // open: Qn, preset, reset
  D_Flip_Flop d_ff_3 (.D(inst[2]), .clk(Clock), .Q(d_ff_1_q[2]));  // open: Qn, preset, reset
  D_Flip_Flop d_ff_4 (.D(inst[3]), .clk(Clock), .Q(d_ff_1_q[3]));  // open: Qn, preset, reset
  D_Flip_Flop d_ff_5 (.D(inst[4]), .clk(Clock), .Q(d_ff_1_q[4]));  // open: Qn, preset, reset
  Adder #(.width(5)) adder_1 (.a(5'b00010), .b(d_ff_1_q), .out(adder_1_out));  // open: cin, cout
  Multiplexer #(.width(5)) multiplexer_1 (.in0(adder_1_out), .in1(d_ff_1_q), .out(inst), .sel(stop));
endmodule

module IR (
  input  [15:0] inst,
  output [3:0] a,
  output [3:0] b_imme,
  output [3:0] c,
  output [3:0] opcode
);


  assign a = inst[7:4];
  assign b_imme = inst[3:0];
  assign c = inst[11:8];
  assign opcode = inst[15:12];
endmodule
