// Logisim project CPU_first_try.circ as structural Verilog: 4 circuits, main circuit implementation
module implementation (
  input  [15:0] Instruction_In,
  input  select_clk,
  input  ClkIn,
  input  in_4,
  output out_5,
  output [4:0] Instruction_Address_Out,
  output [3:0] Reg0_Out,
  output [3:0] Reg1_Out,
  output [3:0] Reg2_Out,
  output [3:0] Reg3_Out,
  output [3:0] Reg4_Out,
  output [3:0] Reg5_Out,
  output [3:0] Reg6_Out,
  output [3:0] Reg7_Out,
  output [3:0] Reg8_Out,
  output [3:0] Reg9_Out,
  output [3:0] Reg10_Out,
  output [3:0] Reg11_Out,
  output [3:0] Reg12_Out,
  output [3:0] Reg13_Out,
  output [3:0] Reg14_Out,
  output [3:0] Reg15_Out
);

  wire and_1_out, undriven_2;
  wire [3:0] A_Value, B_Value, multiplexer_2_out, undriven;

  and and_1 (and_1_out, ClkIn, in_4);
  Multiplexer multiplexer_1 (.in0(ClkIn), .in1(and_1_out), .out(out_5), .sel(select_clk));
  Decoder decoder_1 ();  // open: out0, out1, sel, en
  ALU alu_1 (.B(multiplexer_2_out));  // open: A, Opcode
  Multiplexer #(.width(4)) multiplexer_2 (.in0(undriven), .in1(B_Value), .out(multiplexer_2_out), .sel(undriven_2));
  RegFile regfile_1 (
    .A_Out(A_Value), .B_Out(B_Value), .Reg0_Out(Reg0_Out), .Reg1_Out(Reg1_Out), .Reg2_Out(Reg2_Out),
    .Reg3_Out(Reg3_Out), .Reg4_Out(Reg4_Out), .Reg5_Out(Reg5_Out), .Reg6_Out(Reg6_Out), .Reg7_Out(Reg7_Out),
    .Reg8_Out(Reg8_Out), .Reg9_Out(Reg9_Out), .Reg10_Out(Reg10_Out), .Reg11_Out(Reg11_Out),
    .Reg12_Out(Reg12_Out), .Reg13_Out(Reg13_Out), .Reg14_Out(Reg14_Out), .Reg15_Out(Reg15_Out));  // open: A_Sel_In, B_Sel_In, C_Sel_In, Data_In, Reg_Write_In, clk_in

  // Other names for the same wires on the sheet: Clk = out_5; Instruction[15:0] = Instruction_In;
  //   Opcode[3:0] = Instruction_In[15:12]; Instruction_Address[4:0] = Instruction_Address_Out; Reg0[3:0] = Reg0_Out;
  //   Reg1[3:0] = Reg1_Out; Reg2[3:0] = Reg2_Out; Reg3[3:0] = Reg3_Out; Reg4[3:0] = Reg4_Out; Reg5[3:0] = Reg5_Out;
  //   Reg6[3:0] = Reg6_Out; Reg7[3:0] = Reg7_Out; Reg8[3:0] = Reg8_Out; Reg9[3:0] = Reg9_Out; Reg10[3:0] = Reg10_Out;
  //   Reg11[3:0] = Reg11_Out; Reg12[3:0] = Reg12_Out; Reg13[3:0] = Reg13_Out; Reg14[3:0] = Reg14_Out;
  //   Reg15[3:0] = Reg15_Out
endmodule

module RegFile (
  input  [3:0] A_Sel_In,
  input  [3:0] B_Sel_In,
  input  [3:0] C_Sel_In,
  input  [3:0] Data_In,
  input  Reg_Write_In,
  input  clk_in,
  output [3:0] A_Out,
  output [3:0] B_Out,
  output [3:0] Reg0_Out,
  output [3:0] Reg1_Out,
  output [3:0] Reg2_Out,
  output [3:0] Reg3_Out,
  output [3:0] Reg4_Out,
  output [3:0] Reg5_Out,
  output [3:0] Reg6_Out,
  output [3:0] Reg7_Out,
  output [3:0] Reg8_Out,
  output [3:0] Reg9_Out,
  output [3:0] Reg10_Out,
  output [3:0] Reg11_Out,
  output [3:0] Reg12_Out,
  output [3:0] Reg13_Out,
  output [3:0] Reg14_Out,
  output [3:0] Reg15_Out
);

  wire Reg_Write0, Reg_Write1, Reg_Write2, Reg_Write3, Reg_Write4, Reg_Write5, Reg_Write6, Reg_Write7,
       Reg_Write8, Reg_Write9, Reg_Write10, Reg_Write11, Reg_Write12, Reg_Write13, Reg_Write14, Reg_Write15;

  Demultiplexer #(.select(4)) demultiplexer_1 (
    .out0(Reg_Write0), .out1(Reg_Write1), .out2(Reg_Write2), .out3(Reg_Write3), .out4(Reg_Write4),
    .out5(Reg_Write5), .out6(Reg_Write6), .out7(Reg_Write7), .out8(Reg_Write8), .out9(Reg_Write9),
    .out10(Reg_Write10), .out11(Reg_Write11), .out12(Reg_Write12), .out13(Reg_Write13), .out14(Reg_Write14),
    .out15(Reg_Write15), .in(Reg_Write_In), .sel(C_Sel_In));
  Register #(.width(4)) register_1 (.D(Data_In), .en(Reg_Write0), .clk(clk_in), .Q(Reg0_Out));  // open: clr
  Register #(.width(4)) register_2 (.D(Data_In), .en(Reg_Write4), .clk(clk_in), .Q(Reg4_Out));  // open: clr
  Register #(.width(4)) register_3 (.D(Data_In), .en(Reg_Write8), .clk(clk_in), .Q(Reg8_Out));  // open: clr
  Register #(.width(4)) register_4 (.D(Data_In), .en(Reg_Write12), .clk(clk_in), .Q(Reg12_Out));  // open: clr
  Register #(.width(4)) register_5 (.D(Data_In), .en(Reg_Write1), .clk(clk_in), .Q(Reg1_Out));  // open: clr
  Register #(.width(4)) register_6 (.D(Data_In), .en(Reg_Write5), .clk(clk_in), .Q(Reg5_Out));  // open: clr
  Register #(.width(4)) register_7 (.D(Data_In), .en(Reg_Write9), .clk(clk_in), .Q(Reg9_Out));  // open: clr
  Register #(.width(4)) register_8 (.D(Data_In), .en(Reg_Write13), .clk(clk_in), .Q(Reg13_Out));  // open: clr
  Register #(.width(4)) register_9 (.D(Data_In), .en(Reg_Write2), .clk(clk_in), .Q(Reg2_Out));  // open: clr
  Register #(.width(4)) register_10 (.D(Data_In), .en(Reg_Write6), .clk(clk_in), .Q(Reg6_Out));  // open: clr
  Register #(.width(4)) register_11 (.D(Data_In), .en(Reg_Write10), .clk(clk_in), .Q(Reg10_Out));  // open: clr
  Register #(.width(4)) register_12 (.D(Data_In), .en(Reg_Write14), .clk(clk_in), .Q(Reg14_Out));  // open: clr
  Register #(.width(4)) register_13 (.D(Data_In), .en(Reg_Write3), .clk(clk_in), .Q(Reg3_Out));  // open: clr
  Register #(.width(4)) register_14 (.D(Data_In), .en(Reg_Write7), .clk(clk_in), .Q(Reg7_Out));  // open: clr
  Register #(.width(4)) register_15 (.D(Data_In), .en(Reg_Write11), .clk(clk_in), .Q(Reg11_Out));  // open: clr
  Register #(.width(4)) register_16 (.D(Data_In), .en(Reg_Write15), .clk(clk_in), .Q(Reg15_Out));  // open: clr
  Multiplexer #(.select(4), .width(4)) multiplexer_1 (
    .in0(Reg0_Out), .in1(Reg1_Out), .in2(Reg2_Out), .in3(Reg3_Out), .in4(Reg4_Out), .in5(Reg5_Out),
    .in6(Reg6_Out), .in7(Reg7_Out), .in8(Reg8_Out), .in9(Reg9_Out), .in10(Reg10_Out), .in11(Reg11_Out),
    .in12(Reg12_Out), .in13(Reg13_Out), .in14(Reg14_Out), .in15(Reg15_Out), .out(A_Out), .sel(A_Sel_In));
  Multiplexer #(.select(4), .width(4)) multiplexer_2 (
    .in0(Reg0_Out), .in1(Reg1_Out), .in2(Reg2_Out), .in3(Reg3_Out), .in4(Reg4_Out), .in5(Reg5_Out),
    .in6(Reg6_Out), .in7(Reg7_Out), .in8(Reg8_Out), .in9(Reg9_Out), .in10(Reg10_Out), .in11(Reg11_Out),
    .in12(Reg12_Out), .in13(Reg13_Out), .in14(Reg14_Out), .in15(Reg15_Out), .out(B_Out), .sel(B_Sel_In));

  // Other names for the same wires on the sheet: A[3:0] = A_Out; A_Sel[3:0] = A_Sel_In; B[3:0] = B_Out;
  //   B_Sel[3:0] = B_Sel_In; C_Sel[3:0] = C_Sel_In; clk = clk_in; Data[3:0] = Data_In; Reg0[3:0] = Reg0_Out;
  //   Reg1[3:0] = Reg1_Out; Reg2[3:0] = Reg2_Out; Reg3[3:0] = Reg3_Out; Reg4[3:0] = Reg4_Out; Reg5[3:0] = Reg5_Out;
  //   Reg6[3:0] = Reg6_Out; Reg7[3:0] = Reg7_Out; Reg8[3:0] = Reg8_Out; Reg9[3:0] = Reg9_Out; Reg10[3:0] = Reg10_Out;
  //   Reg11[3:0] = Reg11_Out; Reg12[3:0] = Reg12_Out; Reg13[3:0] = Reg13_Out; Reg14[3:0] = Reg14_Out;
  //   Reg15[3:0] = Reg15_Out; Reg_Write = Reg_Write_In

  // Notes on the sheet:
  //   this C_sel is the register to write to 
endmodule

module ALU (
  input  [3:0] A,
  input  [3:0] B,
  input  [2:0] Opcode
);

  wire [3:0] adder_1_out, adder_2_out, and_1_out, not_1_out, or_1_out, subtractor_1_out, xor_1_out;

  assign not_1_out = ~A;  // NOT_Gate not_1, 4 bits wide
  Adder #(.width(4)) adder_1 (.a(A), .b(B), .out(adder_1_out));  // open: cin, cout
  Subtractor #(.width(4)) subtractor_1 (.a(A), .b(B), .out(subtractor_1_out));  // open: bin, bout
  assign and_1_out = A & B;  // AND_Gate and_1, 4 bits wide
  assign or_1_out = A | B;  // OR_Gate or_1, 4 bits wide
  assign xor_1_out = A ^ B;  // XOR_Gate xor_1, 4 bits wide
  Adder #(.width(4)) adder_2 (.a(not_1_out), .b(4'b0001), .out(adder_2_out));  // open: cin, cout
  Multiplexer #(.select(3), .width(4)) multiplexer_1 (.sel(Opcode));  // open: in0, in1, in2, in3, in4, in5, in6, in7, out

  // Notes on the sheet:
  //   MOVE
endmodule

module Prog_count (
);

  wire Clk;
  wire [15:0] adder_1_out, register_1_q;

  Register #(.width(16)) register_1 (.D(adder_1_out), .en(1'b1), .clk(Clk), .Q(register_1_q), .clr(1'b1));
  Adder #(.width(16)) adder_1 (.a(register_1_q), .b(16'h2), .out(adder_1_out));  // open: cin, cout
endmodule
